// Logisim project 2 out of 3 Logic.circ as structural Verilog: 1 circuit, main circuit main
module main (
  input  A,
  input  B,
  input  C,
  output out_4
);

  wire and_1_out, and_2_out, or_1_out;

  or or_1 (or_1_out, A, B);
  and and_1 (and_1_out, A, B);
  and and_2 (and_2_out, or_1_out, C);
  or or_2 (out_4, and_2_out, and_1_out);

  // Notes on the sheet:
  //   (A+B).C+AB
endmodule
