// Logisim project 8 bit register.circ as structural Verilog: 1 circuit, main circuit main
module main (
  input  D0,
  input  D1,
  input  D2,
  input  D3,
  input  D4,
  input  D5,
  input  D6,
  input  D7,
  output Q0,
  output Q1,
  output Q2,
  output Q3,
  output Q4,
  output Q5,
  output Q6,
  output Q7
);

  wire CLK_out;

  Clock CLK (.out(CLK_out));
  D_Flip_Flop d_ff_1 (.clk(CLK_out), .D(D0), .Q(Q0));  // open: Qn, preset, en, reset
  D_Flip_Flop d_ff_2 (.clk(CLK_out), .D(D1), .Q(Q1));  // open: Qn, preset, en, reset
  D_Flip_Flop d_ff_3 (.clk(CLK_out), .D(D2), .Q(Q2));  // open: Qn, preset, en, reset
  D_Flip_Flop d_ff_4 (.clk(CLK_out), .D(D3), .Q(Q3));  // open: Qn, preset, en, reset
  D_Flip_Flop d_ff_5 (.clk(CLK_out), .D(D4), .Q(Q4));  // open: Qn, preset, en, reset
  D_Flip_Flop d_ff_6 (.clk(CLK_out), .D(D5), .Q(Q5));  // open: Qn, preset, en, reset
  D_Flip_Flop d_ff_7 (.clk(CLK_out), .D(D6), .Q(Q6));  // open: Qn, preset, en, reset
  D_Flip_Flop d_ff_8 (.clk(CLK_out), .D(D7), .Q(Q7));  // open: Qn, preset, en, reset
endmodule
