// Logisim project AND OR NAND NOR XOR XNOR NOT and ADD.circ as structural Verilog: 1 circuit, main circuit main
module main (
  input  [3:0] in_1,
  input  A,
  input  B,
  input  in_4,
  output Result,
  output out_6
);

  wire adder_1_out, AND_out, NAND_out, NOR_out, NOT_out, OR_out, XNOR_out, XOR_out;

  nand NAND (NAND_out, A, B);
  not NOT (NOT_out, A);
  and AND (AND_out, A, B);
  or OR (OR_out, A, B);
  xor XOR (XOR_out, A, B);
  nor NOR (NOR_out, A, B);
  Adder #(.width(1)) adder_1 (.a(A), .b(B), .out(adder_1_out), .cin(in_4), .cout(out_6));
  Multiplexer #(.select(4), .enable("false")) multiplexer_1 (
    .in0(NAND_out), .in1(XNOR_out), .in5(NOT_out), .in7(AND_out), .in9(OR_out), .in11(XOR_out),
    .in13(NOR_out), .in15(adder_1_out), .out(Result), .sel(in_1));  // open: in2, in3, in4, in6, in8, in10, in12, in14
  xnor XNOR (XNOR_out, A, B);
endmodule
