// Logisim project Addition using single bits and full adder.circ as structural Verilog: 1 circuit, main circuit main
module main (
  input  A0,
  input  B0,
  input  A1,
  input  B1,
  input  A2,
  input  B2,
  output C0,
  output C1,
  output C2,
  output C
);

  wire adder_1_cout, adder_2_cout;

  Adder #(.width(1)) adder_1 (.a(A0), .b(B0), .out(C0), .cout(adder_1_cout));  // open: cin
  Adder #(.width(1)) adder_2 (.a(A1), .b(B1), .out(C1), .cin(adder_1_cout), .cout(adder_2_cout));
  Adder #(.width(1)) adder_3 (.a(A2), .b(B2), .out(C2), .cin(adder_2_cout), .cout(C));
endmodule
