// Logisim project Comparator.circ as structural Verilog: 1 circuit, main circuit main
module main (
  input  [3:0] A,
  input  [3:0] B,
  output Greater,
  output Equal,
  output Less_than
);

  Comparator #(.width(4)) comparator_1 (.a(A), .b(B), .gt(Greater), .eq(Equal), .lt(Less_than));
endmodule
