// Logisim project Subtract and multiply.circ as structural Verilog: 1 circuit, main circuit main
module main (
  input  in_1,
  input  A,
  input  B,
  input  in_4,
  output out_5,
  output out_6,
  output out_7
);

  Subtractor #(.width(1)) subtractor_1 (.a(A), .b(B), .out(out_5), .bin(in_1), .bout(out_6));
  Multiplier #(.width(1)) multiplier_1 (.a(A), .b(B), .out(out_7), .cin(in_4));  // open: cout
endmodule
