// Logisim project Tri state buffer.circ as structural Verilog: 1 circuit, main circuit main
module main (
  input  in_1,
  input  in_2,
  input  in_3,
  input  in_4,
  output out_5,
  output out_6
);

  assign out_5 = in_1 ? in_2 : 1'bz;  // Controlled_Buffer controlled_buffer_1
  assign out_6 = in_3 ? ~in_4 : 1'bz;  // Controlled_Inverter controlled_inverter_1
endmodule
