// Logisim project flip flop.circ as structural Verilog: 1 circuit, main circuit main
module main (
  input  D,
  output Q,
  output Q_Bar
);

  wire CLK_out;

  Clock CLK (.out(CLK_out));
  D_Flip_Flop d_ff_1 (.clk(CLK_out), .D(D), .Q(Q), .Qn(Q_Bar));  // open: preset, en, reset

  // Notes on the sheet:
  //   Rising edge is when the clock output changes from 0 to 1
  //   Every other state of the clock, the value of Q stays unchanged
  //   Only on the rising edge of the clock the value of D passes to Q
endmodule
